// Logisim project Circuito de entradas de dados.circ as structural Verilog: 8 circuits, main circuit main
module main (
  input  A0,
  input  A1,
  input  A2,
  input  A3,
  input  A4,
  input  A5,
  input  in_7,
  input  in_8,
  input  A6,
  output out_10,
  output out_11,
  output out_12,
  output out_13,
  output out_14,
  output out_15,
  output out_16,
  output out_17,
  output out_18,
  output out_19,
  output out_20,
  output out_21,
  output out_22
);

  wire undriven, undriven_2, undriven_3, undriven_4, undriven_5, undriven_6, undriven_7, undriven_8;

  conversor_binario_bcd conversor_binario_bcd_1 (
    .A(A0), .B(A1), .C(A2), .D(A3), .E(A4), .F(A5), .G(A6), .n0(out_10), .n1(out_11), .n2(out_13),
    .n3(out_15), .n4(out_17), .n5(out_19), .N6(out_20), .n7(out_21), .N8(out_22));
  mux4x2 mux4x2_1 (
    .B3(undriven), .A3(undriven_2), .B2(undriven_3), .A2(undriven_4), .B1(undriven_5), .A1(undriven_6),
    .B0(undriven_7), .A0(undriven_8), .S(in_7), .E(in_8), .out_11(out_12), .out_12(out_14), .out_13(out_16),
    .out_14(out_18));
endmodule

module Somador1bt (
  input  Ci,
  input  A,
  input  B,
  output S,
  output Co
);

  wire and_1_out, and_2_out, and_3_out, xor_1_out;

  xor xor_1 (xor_1_out, B, Ci);
  and and_1 (and_1_out, A, B);
  and and_2 (and_2_out, A, Ci);
  and and_3 (and_3_out, B, Ci);
  xor xor_2 (S, A, xor_1_out);
  or or_1 (Co, and_1_out, and_2_out, and_3_out);
endmodule

module Botoes (
  input  A,
  input  B,
  input  C,
  input  Ch0,
  output N0,
  output N1,
  output out_7
);

  wire not_1_out, not_2_out, xor_1_out, xor_2_out;

  xor xor_1 (xor_1_out, A, B);
  not not_1 (not_1_out, C);
  not not_2 (not_2_out, B);
  xor xor_2 (xor_2_out, A, C);
  and and_1 (N0, xor_1_out, not_1_out);
  and and_2 (N1, not_2_out, xor_2_out);

  assign out_7 = Ch0;
endmodule

module Somador7bts (
  input  Ci,
  input  A0,
  input  B0,
  input  A1,
  input  B1,
  input  A2,
  input  B2,
  input  A3,
  input  B3,
  input  A4,
  input  B4,
  input  A5,
  input  B5,
  input  A6,
  input  B6,
  output S0,
  output S1,
  output S2,
  output S3,
  output S4,
  output S5,
  output S6,
  output Cout
);

  wire somador1bt_1_co, somador1bt_2_co, somador1bt_3_co, somador1bt_4_co, somador1bt_5_co, somador1bt_6_co;

  Somador1bt somador1bt_1 (.Ci(Ci), .A(A0), .B(B0), .S(S0), .Co(somador1bt_1_co));
  Somador1bt somador1bt_2 (.Ci(somador1bt_1_co), .A(A1), .B(B1), .S(S1), .Co(somador1bt_2_co));
  Somador1bt somador1bt_3 (.Ci(somador1bt_2_co), .A(A2), .B(B2), .S(S2), .Co(somador1bt_3_co));
  Somador1bt somador1bt_4 (.Ci(somador1bt_3_co), .A(A3), .B(B3), .S(S3), .Co(somador1bt_4_co));
  Somador1bt somador1bt_5 (.Ci(somador1bt_4_co), .A(A4), .B(B4), .S(S4), .Co(somador1bt_5_co));
  Somador1bt somador1bt_6 (.Ci(somador1bt_5_co), .A(A5), .B(B5), .S(S5), .Co(somador1bt_6_co));
  Somador1bt somador1bt_7 (.Ci(somador1bt_6_co), .A(A6), .B(B6), .S(S6), .Co(Cout));
endmodule

module Somador_Subtrator (
  input  Ci,
  input  A0,
  input  B0,
  input  A1,
  input  B1,
  input  A2,
  input  B2,
  input  A3,
  input  B3,
  input  A4,
  input  B4,
  input  A5,
  input  B5,
  input  A6,
  input  B6,
  output S0,
  output S1,
  output S2,
  output S3,
  output S4,
  output S5,
  output S6,
  output Cout
);

  wire xor_1_out, xor_2_out, xor_3_out, xor_4_out, xor_5_out, xor_6_out, xor_7_out;

  xor xor_1 (xor_1_out, B0, Ci);
  xor xor_2 (xor_2_out, B1, Ci);
  xor xor_3 (xor_3_out, B2, Ci);
  xor xor_4 (xor_4_out, B3, Ci);
  xor xor_5 (xor_5_out, B4, Ci);
  xor xor_6 (xor_6_out, B5, Ci);
  xor xor_7 (xor_7_out, B6, Ci);
  Somador7bts somador7bts_1 (
    .Ci(Ci), .A0(A0), .B0(xor_1_out), .A1(A1), .B1(xor_2_out), .A2(A2), .B2(xor_3_out), .A3(A3),
    .B3(xor_4_out), .A4(A4), .B4(xor_5_out), .A5(A5), .B5(xor_6_out), .A6(A6), .B6(xor_7_out), .S0(S0),
    .S1(S1), .S2(S2), .S3(S3), .S4(S4), .S5(S5), .S6(S6), .Cout(Cout));
endmodule

module Entradas_e_Somas (
  input  Bt2,
  input  Bt1,
  input  Bt0,
  input  Chave,
  input  A0,
  input  A1,
  input  A2,
  input  B2,
  input  A3,
  input  B3,
  input  A4,
  input  B4,
  input  A5,
  input  B5,
  input  A6,
  input  B6,
  output S0,
  output S1,
  output S2,
  output S3,
  output S4,
  output S5,
  output S6,
  output Cout
);

  wire botoes_1_n0, botoes_1_n1, botoes_1_out_7;

  Botoes botoes_1 (.A(Bt2), .B(Bt1), .C(Bt0), .Ch0(Chave), .N0(botoes_1_n0), .N1(botoes_1_n1), .out_7(botoes_1_out_7));
  Somador_Subtrator somador_subtrator_1 (
    .Ci(botoes_1_out_7), .A0(A0), .B0(botoes_1_n0), .A1(A1), .B1(botoes_1_n1), .A2(A2), .B2(B2), .A3(A3),
    .B3(B3), .A4(A4), .B4(B4), .A5(A5), .B5(B5), .A6(A6), .B6(B6), .S0(S0), .S1(S1), .S2(S2), .S3(S3),
    .S4(S4), .S5(S5), .S6(S6), .Cout(Cout));

  // Notes on the sheet:
  //   N3
  //   N1
  //   N2
endmodule

module conversor_binario_bcd (
  input  A,
  input  B,
  input  C,
  input  D,
  input  E,
  input  F,
  input  G,
  output n0,
  output n1,
  output n2,
  output n3,
  output n4,
  output n5,
  output N6,
  output n7,
  output N8
);

  wire and_1_out, and_2_out, and_3_out, and_4_out, and_5_out, and_6_out, and_7_out, and_8_out, and_9_out,
       and_10_out, and_11_out, and_12_out, and_13_out, and_14_out, and_15_out, and_16_out, and_17_out,
       and_18_out, and_19_out, and_20_out, and_21_out, and_22_out, and_23_out, and_24_out, and_25_out,
       and_26_out, and_27_out, and_28_out, and_29_out, and_30_out, and_31_out, and_32_out, and_33_out,
       and_34_out, and_35_out, and_36_out, and_37_out, and_38_out, and_39_out, and_40_out, and_41_out,
       and_42_out, and_43_out, and_44_out, and_45_out, and_46_out, and_47_out, and_48_out, and_49_out,
       and_50_out, and_51_out, and_52_out, and_53_out, and_54_out, and_55_out, and_56_out, and_57_out,
       and_58_out, and_59_out, and_60_out, and_61_out, and_62_out, and_63_out, and_64_out, and_65_out,
       and_66_out, and_67_out;

  and and_1 (and_1_out, A, ~B, ~C);  // AND_Gate
  and and_2 (and_2_out, ~A, B, C);  // AND_Gate
  and and_3 (and_3_out, ~A, B, D);  // AND_Gate
  and and_4 (and_4_out, ~A, B, ~C, ~D);  // AND_Gate
  and and_5 (and_5_out, ~A, C, D, E);  // AND_Gate
  and and_6 (and_6_out, A, ~B, ~C);  // AND_Gate
  and and_7 (and_7_out, ~A, ~B, C, D);  // AND_Gate
  and and_8 (and_8_out, ~A, ~B, C, E);  // AND_Gate
  and and_9 (and_9_out, ~A, B, ~D, F);  // AND_Gate
  and and_10 (and_10_out, A, ~C, ~D, E, F);  // AND_Gate
  and and_11 (and_11_out, A, ~C, D, ~E, ~F);  // AND_Gate
  and and_12 (and_12_out, ~A, ~B, C, ~D, ~E);  // AND_Gate
  and and_13 (and_13_out, ~A, B, C, D, ~E);  // AND_Gate
  and and_14 (and_14_out, ~A, B, ~D, E);  // AND_Gate
  and and_15 (and_15_out, A, ~B, D, F);  // AND_Gate
  and and_16 (and_16_out, B, ~C, ~D);  // AND_Gate
  and and_17 (and_17_out, ~B, D, E, F);  // AND_Gate
  and and_18 (and_18_out, ~B, ~C, D, E);  // AND_Gate
  and and_19 (and_19_out, ~B, ~C, D, F);  // AND_Gate
  and and_20 (and_20_out, ~A, ~B, C, D, E, ~F);  // AND_Gate
  and and_21 (and_21_out, ~A, ~B, C, ~D, ~E, F);  // AND_Gate
  and and_22 (and_22_out, ~A, B, C, D, ~E, F);  // AND_Gate
  and and_23 (and_23_out, A, ~B, C, D, ~E, ~F);  // AND_Gate
  and and_24 (and_24_out, ~A, B, C, ~D, ~E, ~F);  // AND_Gate
  and and_25 (and_25_out, A, ~B, ~C, D, E, F);  // AND_Gate
  and and_26 (and_26_out, ~A, ~B, ~C, D, ~E, ~F);  // AND_Gate
  and and_27 (and_27_out, B, ~C, ~D, E, F);  // AND_Gate
  and and_28 (and_28_out, A, ~C, ~D, E, ~F);  // AND_Gate
  and and_29 (and_29_out, A, B, ~C, D, ~E, ~F);  // AND_Gate
  and and_30 (and_30_out, A, B, ~C, ~D, F);  // AND_Gate
  and and_31 (and_31_out, ~A, ~C, ~D, E, ~F);  // AND_Gate
  and and_32 (and_32_out, ~A, ~B, ~C, E, F);  // AND_Gate
  and and_33 (and_33_out, ~A, B, ~C, D, E);  // AND_Gate
  and and_34 (and_34_out, ~A, C, D, ~E, ~F);  // AND_Gate
  and and_35 (and_35_out, A, ~C, ~D, ~E, ~F);  // AND_Gate
  and and_36 (and_36_out, A, ~B, C, E, F);  // AND_Gate
  and and_37 (and_37_out, A, ~B, C, ~D, E);  // AND_Gate
  and and_38 (and_38_out, A, ~B, ~C, ~E, F);  // AND_Gate
  and and_39 (and_39_out, ~A, ~B, C, ~E, ~F);  // AND_Gate
  and and_40 (and_40_out, A, ~B, D, E);  // AND_Gate
  and and_41 (and_41_out, ~A, B, C, ~D, E, F);  // AND_Gate
  and and_42 (and_42_out, ~A, B, ~C, ~D, ~E, F);  // AND_Gate
  and and_43 (and_43_out, ~A, ~B, C, D, ~E);  // AND_Gate
  and and_44 (and_44_out, A, ~B, ~C, D, E, ~F);  // AND_Gate
  and and_45 (and_45_out, ~B, ~C, ~D, ~E, F);  // AND_Gate
  and and_46 (and_46_out, ~A, ~B, ~D, E, F);  // AND_Gate
  and and_47 (and_47_out, A, ~B, C, ~D, F);  // AND_Gate
  and and_48 (and_48_out, B, ~C, ~D, ~E, ~F);  // AND_Gate
  and and_49 (and_49_out, A, ~B, D, E, ~F);  // AND_Gate
  and and_50 (and_50_out, A, ~B, ~C, D, ~F);  // AND_Gate
  and and_51 (and_51_out, ~A, B, C, D, ~E, ~F);  // AND_Gate
  and and_52 (and_52_out, ~A, B, D, E, F);  // AND_Gate
  and and_53 (and_53_out, ~A, B, ~D, E, ~F);  // AND_Gate
  and and_54 (and_54_out, ~A, B, ~C, D, F);  // AND_Gate
  and and_55 (and_55_out, ~A, ~B, C, D, ~E, F);  // AND_Gate
  and and_56 (and_56_out, ~B, ~C, D, E, ~F);  // AND_Gate
  and and_57 (and_57_out, A, B, ~C, D, ~E, ~F);  // AND_Gate
  and and_58 (and_58_out, A, B, ~C, ~D, E);  // AND_Gate
  and and_59 (and_59_out, ~B, G);  // AND_Gate
  and and_60 (and_60_out, ~A, G);  // AND_Gate
  and and_61 (and_61_out, ~C, ~D, G);  // AND_Gate
  or or_1 (n2, and_1_out, and_2_out, and_3_out);
  and and_62 (and_62_out, ~A, ~B, C, ~D, ~E, ~F);  // AND_Gate
  or or_2 (n3, and_4_out, and_5_out, and_6_out, and_7_out, and_8_out);
  or or_3 (n4, and_9_out, and_10_out, and_11_out, and_40_out, and_12_out, and_13_out, and_14_out, and_15_out, and_16_out, and_17_out, and_18_out, and_19_out);
  or or_4 (n5, and_20_out, and_21_out, and_22_out, and_23_out, and_24_out, and_25_out, and_26_out, and_27_out, and_28_out, and_29_out, and_30_out);
  or or_5 (N8, and_57_out, and_58_out, and_59_out, and_60_out, and_61_out);
  and and_63 (and_63_out, A, B, ~C, D, ~E, ~F);  // AND_Gate
  and and_64 (and_64_out, A, B, ~C, ~D, E);  // AND_Gate
  and and_65 (and_65_out, A, B, ~C, ~E, ~F);  // AND_Gate
  and and_66 (and_66_out, A, B, ~C, ~D);  // AND_Gate
  and and_67 (and_67_out, A, ~B, C);  // AND_Gate
  or or_6 (n0, and_63_out, and_64_out);
  or or_7 (n1, and_65_out, and_66_out, and_67_out);
  or or_8 (n7, and_45_out, and_46_out, and_47_out, and_48_out, and_49_out, and_50_out, and_51_out, and_52_out, and_53_out, and_54_out, and_55_out, and_62_out, and_56_out);
  or or_9 (N6, and_31_out, and_32_out, and_33_out, and_34_out, and_35_out, and_41_out, and_36_out, and_37_out, and_42_out, and_38_out, and_43_out, and_39_out, and_44_out);
endmodule

module mux4x2 (
  input  B3,
  input  A3,
  input  B2,
  input  A2,
  input  B1,
  input  A1,
  input  B0,
  input  A0,
  input  S,
  input  E,
  output out_11,
  output out_12,
  output out_13,
  output out_14
);

  wire and_1_out, and_2_out, and_3_out, and_4_out, and_5_out, and_6_out, and_7_out, and_8_out, not_1_out,
       not_2_out, not_3_out;

  not not_1 (not_1_out, not_2_out);
  not not_2 (not_2_out, S);
  not not_3 (not_3_out, E);
  and and_1 (and_1_out, B3, not_2_out, not_3_out);
  and and_2 (and_2_out, A3, not_1_out, not_3_out);
  and and_3 (and_3_out, B2, not_2_out, not_3_out);
  and and_4 (and_4_out, A2, not_1_out, not_3_out);
  and and_5 (and_5_out, B1, not_2_out, not_3_out);
  and and_6 (and_6_out, A1, not_1_out, not_3_out);
  and and_7 (and_7_out, B0, not_2_out, not_3_out);
  and and_8 (and_8_out, A0, not_1_out, not_3_out);
  or or_1 (out_11, and_1_out, and_2_out);
  or or_2 (out_12, and_3_out, and_4_out);
  or or_3 (out_13, and_5_out, and_6_out);
  or or_4 (out_14, and_7_out, and_8_out);
endmodule
