// Logisim project Circuito de entradas de dados.circ as structural Verilog: 12 circuits, main circuit Somador1bt
module main (
  input  A6,
  input  A6_2,
  input  A5,
  input  A4,
  input  A3,
  input  A2,
  input  A1,
  input  A0,
  input  A6_3,
  input  in_10,
  input  A5_2,
  input  A4_2,
  input  A3_2,
  input  A2_2,
  input  A1_2,
  input  A0_2,
  output out_17,
  output S3,
  output S2,
  output S1,
  output S0
);

  wire conversor_binario_bcd_1_n1, conversor_binario_bcd_1_n2, conversor_binario_bcd_1_n3,
       conversor_binario_bcd_1_n4, conversor_binario_bcd_1_n5, conversor_binario_bcd_1_n6,
       conversor_binario_bcd_1_n7, conversor_binario_bcd_1_n8, somador_subtrator_1_s0,
       somador_subtrator_1_s1, somador_subtrator_1_s2, somador_subtrator_1_s3, somador_subtrator_1_s4,
       somador_subtrator_1_s5, somador_subtrator_1_s6;

  Somador_Subtrator somador_subtrator_1 (
    .Ci(A6), .A0(A0), .B0(A0_2), .A1(A1), .B1(A1_2), .A2(A2), .B2(A2_2), .A3(A3), .B3(A3_2), .A4(A4),
    .B4(A4_2), .A5(A5), .B5(A5_2), .A6(A6_2), .B6(A6_3), .S0(somador_subtrator_1_s0),
    .S1(somador_subtrator_1_s1), .S2(somador_subtrator_1_s2), .S3(somador_subtrator_1_s3),
    .S4(somador_subtrator_1_s4), .S5(somador_subtrator_1_s5), .S6(somador_subtrator_1_s6));  // open: Cout
  conversor_binario_bcd conversor_binario_bcd_1 (
    .A(somador_subtrator_1_s6), .B(somador_subtrator_1_s5), .C(somador_subtrator_1_s4),
    .D(somador_subtrator_1_s3), .E(somador_subtrator_1_s2), .F(somador_subtrator_1_s1),
    .G(somador_subtrator_1_s0), .n0(out_17), .n1(conversor_binario_bcd_1_n1),
    .n2(conversor_binario_bcd_1_n2), .n3(conversor_binario_bcd_1_n3), .n4(conversor_binario_bcd_1_n4),
    .n5(conversor_binario_bcd_1_n5), .N6(conversor_binario_bcd_1_n6), .n7(conversor_binario_bcd_1_n7),
    .N8(conversor_binario_bcd_1_n8));
  mux4x2 mux4x2_1 (
    .A0(conversor_binario_bcd_1_n1), .B0(conversor_binario_bcd_1_n5), .A1(conversor_binario_bcd_1_n2),
    .B1(conversor_binario_bcd_1_n6), .A2(conversor_binario_bcd_1_n3), .B2(conversor_binario_bcd_1_n7),
    .A3(conversor_binario_bcd_1_n4), .B3(conversor_binario_bcd_1_n8), .S(in_10), .S0(S3), .S1(S2), .S2(S1),
    .S3(S0));
endmodule

module Somador1bt (
  input  Ci,
  input  A,
  input  B,
  output S,
  output Co
);

  wire and_1_out, and_2_out, and_3_out, xor_1_out;

  xor xor_1 (xor_1_out, B, Ci);
  and and_1 (and_1_out, A, B);
  and and_2 (and_2_out, A, Ci);
  and and_3 (and_3_out, B, Ci);
  xor xor_2 (S, A, xor_1_out);
  or or_1 (Co, and_1_out, and_2_out, and_3_out);
endmodule

module Botoes (
  input  A,
  input  B,
  input  C,
  input  Ch0,
  output N0,
  output N1,
  output out_7
);

  wire not_1_out, not_2_out, xor_1_out, xor_2_out;

  xor xor_1 (xor_1_out, A, B);
  not not_1 (not_1_out, C);
  not not_2 (not_2_out, B);
  xor xor_2 (xor_2_out, A, C);
  and and_1 (N0, xor_1_out, not_1_out);
  and and_2 (N1, not_2_out, xor_2_out);

  assign out_7 = Ch0;
endmodule

module Somador7bts (
  input  Ci,
  input  A0,
  input  B0,
  input  A1,
  input  B1,
  input  A2,
  input  B2,
  input  A3,
  input  B3,
  input  A4,
  input  B4,
  input  A5,
  input  B5,
  input  A6,
  input  B6,
  output S0,
  output S1,
  output S2,
  output S3,
  output S4,
  output S5,
  output S6,
  output Cout
);

  wire somador1bt_1_co, somador1bt_2_co, somador1bt_3_co, somador1bt_4_co, somador1bt_5_co, somador1bt_6_co;

  Somador1bt somador1bt_1 (.Ci(Ci), .A(A0), .B(B0), .S(S0), .Co(somador1bt_1_co));
  Somador1bt somador1bt_2 (.Ci(somador1bt_1_co), .A(A1), .B(B1), .S(S1), .Co(somador1bt_2_co));
  Somador1bt somador1bt_3 (.Ci(somador1bt_2_co), .A(A2), .B(B2), .S(S2), .Co(somador1bt_3_co));
  Somador1bt somador1bt_4 (.Ci(somador1bt_3_co), .A(A3), .B(B3), .S(S3), .Co(somador1bt_4_co));
  Somador1bt somador1bt_5 (.Ci(somador1bt_4_co), .A(A4), .B(B4), .S(S4), .Co(somador1bt_5_co));
  Somador1bt somador1bt_6 (.Ci(somador1bt_5_co), .A(A5), .B(B5), .S(S5), .Co(somador1bt_6_co));
  Somador1bt somador1bt_7 (.Ci(somador1bt_6_co), .A(A6), .B(B6), .S(S6), .Co(Cout));
endmodule

module Somador_Subtrator (
  input  Ci,
  input  A0,
  input  B0,
  input  A1,
  input  B1,
  input  A2,
  input  B2,
  input  A3,
  input  B3,
  input  A4,
  input  B4,
  input  A5,
  input  B5,
  input  A6,
  input  B6,
  output S0,
  output S1,
  output S2,
  output S3,
  output S4,
  output S5,
  output S6,
  output Cout
);

  wire xor_1_out, xor_2_out, xor_3_out, xor_4_out, xor_5_out, xor_6_out, xor_7_out;

  xor xor_1 (xor_1_out, B0, Ci);
  xor xor_2 (xor_2_out, B1, Ci);
  xor xor_3 (xor_3_out, B2, Ci);
  xor xor_4 (xor_4_out, B3, Ci);
  xor xor_5 (xor_5_out, B4, Ci);
  xor xor_6 (xor_6_out, B5, Ci);
  xor xor_7 (xor_7_out, B6, Ci);
  Somador7bts somador7bts_1 (
    .Ci(Ci), .A0(A0), .B0(xor_1_out), .A1(A1), .B1(xor_2_out), .A2(A2), .B2(xor_3_out), .A3(A3),
    .B3(xor_4_out), .A4(A4), .B4(xor_5_out), .A5(A5), .B5(xor_6_out), .A6(A6), .B6(xor_7_out), .S0(S0),
    .S1(S1), .S2(S2), .S3(S3), .S4(S4), .S5(S5), .S6(S6), .Cout(Cout));
endmodule

module Entradas_e_Somas (
  input  Bt2,
  input  Bt1,
  input  Bt0,
  input  Chave,
  input  A0,
  input  A1,
  input  A2,
  input  B2,
  input  A3,
  input  B3,
  input  A4,
  input  B4,
  input  A5,
  input  B5,
  input  A6,
  input  B6,
  output S0,
  output S1,
  output S2,
  output S3,
  output S4,
  output S5,
  output S6,
  output Cout
);

  wire botoes_1_n0, botoes_1_n1, botoes_1_out_7;

  Botoes botoes_1 (.A(Bt2), .B(Bt1), .C(Bt0), .Ch0(Chave), .N0(botoes_1_n0), .N1(botoes_1_n1), .out_7(botoes_1_out_7));
  Somador_Subtrator somador_subtrator_1 (
    .Ci(botoes_1_out_7), .A0(A0), .B0(botoes_1_n0), .A1(A1), .B1(botoes_1_n1), .A2(A2), .B2(B2), .A3(A3),
    .B3(B3), .A4(A4), .B4(B4), .A5(A5), .B5(B5), .A6(A6), .B6(B6), .S0(S0), .S1(S1), .S2(S2), .S3(S3),
    .S4(S4), .S5(S5), .S6(S6), .Cout(Cout));

  // Notes on the sheet:
  //   N3
  //   N1
  //   N2
endmodule

module conversor_binario_bcd (
  input  A,
  input  B,
  input  C,
  input  D,
  input  E,
  input  F,
  input  G,
  output n0,
  output n1,
  output n2,
  output n3,
  output n4,
  output n5,
  output N6,
  output n7,
  output N8
);

  wire and_1_out, and_2_out, and_3_out, and_4_out, and_5_out, and_6_out, and_7_out, and_8_out, and_9_out,
       and_10_out, and_11_out, and_12_out, and_13_out, and_14_out, and_15_out, and_16_out, and_17_out,
       and_18_out, and_19_out, and_20_out, and_21_out, and_22_out, and_23_out, and_24_out, and_25_out,
       and_26_out, and_27_out, and_28_out, and_29_out, and_30_out, and_31_out, and_32_out, and_33_out,
       and_34_out, and_35_out, and_36_out, and_37_out, and_38_out, and_39_out, and_40_out, and_41_out,
       and_42_out, and_43_out, and_44_out, and_45_out, and_46_out, and_47_out, and_48_out, and_49_out,
       and_50_out, and_51_out, and_52_out, and_53_out, and_54_out, and_55_out, and_56_out, and_57_out,
       and_58_out, and_59_out, and_60_out, and_61_out, and_62_out, and_63_out, and_64_out, and_65_out,
       and_66_out, and_67_out;

  and and_1 (and_1_out, A, ~B, ~C);  // AND_Gate
  and and_2 (and_2_out, ~A, B, C);  // AND_Gate
  and and_3 (and_3_out, ~A, B, D);  // AND_Gate
  and and_4 (and_4_out, ~A, B, ~C, ~D);  // AND_Gate
  and and_5 (and_5_out, ~A, C, D, E);  // AND_Gate
  and and_6 (and_6_out, A, ~B, ~C);  // AND_Gate
  and and_7 (and_7_out, ~A, ~B, C, D);  // AND_Gate
  and and_8 (and_8_out, ~A, ~B, C, E);  // AND_Gate
  and and_9 (and_9_out, ~A, B, ~D, F);  // AND_Gate
  and and_10 (and_10_out, A, ~C, ~D, E, F);  // AND_Gate
  and and_11 (and_11_out, A, ~C, D, ~E, ~F);  // AND_Gate
  and and_12 (and_12_out, ~A, ~B, C, ~D, ~E);  // AND_Gate
  and and_13 (and_13_out, ~A, B, C, D, ~E);  // AND_Gate
  and and_14 (and_14_out, ~A, B, ~D, E);  // AND_Gate
  and and_15 (and_15_out, A, ~B, D, F);  // AND_Gate
  and and_16 (and_16_out, B, ~C, ~D);  // AND_Gate
  and and_17 (and_17_out, ~B, D, E, F);  // AND_Gate
  and and_18 (and_18_out, ~B, ~C, D, E);  // AND_Gate
  and and_19 (and_19_out, ~B, ~C, D, F);  // AND_Gate
  and and_20 (and_20_out, ~A, ~B, C, D, E, ~F);  // AND_Gate
  and and_21 (and_21_out, ~A, ~B, C, ~D, ~E, F);  // AND_Gate
  and and_22 (and_22_out, ~A, B, C, D, ~E, F);  // AND_Gate
  and and_23 (and_23_out, A, ~B, C, D, ~E, ~F);  // AND_Gate
  and and_24 (and_24_out, ~A, B, C, ~D, ~E, ~F);  // AND_Gate
  and and_25 (and_25_out, A, ~B, ~C, D, E, F);  // AND_Gate
  and and_26 (and_26_out, ~A, ~B, ~C, D, ~E, ~F);  // AND_Gate
  and and_27 (and_27_out, B, ~C, ~D, E, F);  // AND_Gate
  and and_28 (and_28_out, A, ~C, ~D, E, ~F);  // AND_Gate
  and and_29 (and_29_out, A, B, ~C, D, ~E, ~F);  // AND_Gate
  and and_30 (and_30_out, A, B, ~C, ~D, F);  // AND_Gate
  and and_31 (and_31_out, ~A, ~C, ~D, E, ~F);  // AND_Gate
  and and_32 (and_32_out, ~A, ~B, ~C, E, F);  // AND_Gate
  and and_33 (and_33_out, ~A, B, ~C, D, E);  // AND_Gate
  and and_34 (and_34_out, ~A, C, D, ~E, ~F);  // AND_Gate
  and and_35 (and_35_out, A, ~C, ~D, ~E, ~F);  // AND_Gate
  and and_36 (and_36_out, A, ~B, C, E, F);  // AND_Gate
  and and_37 (and_37_out, A, ~B, C, ~D, E);  // AND_Gate
  and and_38 (and_38_out, A, ~B, ~C, ~E, F);  // AND_Gate
  and and_39 (and_39_out, ~A, ~B, C, ~E, ~F);  // AND_Gate
  and and_40 (and_40_out, A, ~B, D, E);  // AND_Gate
  and and_41 (and_41_out, ~A, B, C, ~D, E, F);  // AND_Gate
  and and_42 (and_42_out, ~A, B, ~C, ~D, ~E, F);  // AND_Gate
  and and_43 (and_43_out, ~A, ~B, C, D, ~E);  // AND_Gate
  and and_44 (and_44_out, A, ~B, ~C, D, E, ~F);  // AND_Gate
  and and_45 (and_45_out, ~B, ~C, ~D, ~E, F);  // AND_Gate
  and and_46 (and_46_out, ~A, ~B, ~D, E, F);  // AND_Gate
  and and_47 (and_47_out, A, ~B, C, ~D, F);  // AND_Gate
  and and_48 (and_48_out, B, ~C, ~D, ~E, ~F);  // AND_Gate
  and and_49 (and_49_out, A, ~B, D, E, ~F);  // AND_Gate
  and and_50 (and_50_out, A, ~B, ~C, D, ~F);  // AND_Gate
  and and_51 (and_51_out, ~A, B, C, D, ~E, ~F);  // AND_Gate
  and and_52 (and_52_out, ~A, B, D, E, F);  // AND_Gate
  and and_53 (and_53_out, ~A, B, ~D, E, ~F);  // AND_Gate
  and and_54 (and_54_out, ~A, B, ~C, D, F);  // AND_Gate
  and and_55 (and_55_out, ~A, ~B, C, D, ~E, F);  // AND_Gate
  and and_56 (and_56_out, ~B, ~C, D, E, ~F);  // AND_Gate
  and and_57 (and_57_out, A, B, ~C, D, ~E, ~F);  // AND_Gate
  and and_58 (and_58_out, A, B, ~C, ~D, E);  // AND_Gate
  and and_59 (and_59_out, ~B, G);  // AND_Gate
  and and_60 (and_60_out, ~A, G);  // AND_Gate
  and and_61 (and_61_out, ~C, ~D, G);  // AND_Gate
  or or_1 (n2, and_1_out, and_2_out, and_3_out);
  and and_62 (and_62_out, ~A, ~B, C, ~D, ~E, ~F);  // AND_Gate
  or or_2 (n3, and_4_out, and_5_out, and_6_out, and_7_out, and_8_out);
  or or_3 (n4, and_9_out, and_10_out, and_11_out, and_40_out, and_12_out, and_13_out, and_14_out, and_15_out, and_16_out, and_17_out, and_18_out, and_19_out);
  or or_4 (n5, and_20_out, and_21_out, and_22_out, and_23_out, and_24_out, and_25_out, and_26_out, and_27_out, and_28_out, and_29_out, and_30_out);
  or or_5 (N8, and_57_out, and_58_out, and_59_out, and_60_out, and_61_out);
  and and_63 (and_63_out, A, B, ~C, D, ~E, ~F);  // AND_Gate
  and and_64 (and_64_out, A, B, ~C, ~D, E);  // AND_Gate
  and and_65 (and_65_out, A, B, ~C, ~E, ~F);  // AND_Gate
  and and_66 (and_66_out, A, B, ~C, ~D);  // AND_Gate
  and and_67 (and_67_out, A, ~B, C);  // AND_Gate
  or or_6 (n0, and_63_out, and_64_out);
  or or_7 (n1, and_65_out, and_66_out, and_67_out);
  or or_8 (n7, and_45_out, and_46_out, and_47_out, and_48_out, and_49_out, and_50_out, and_51_out, and_52_out, and_53_out, and_54_out, and_55_out, and_62_out, and_56_out);
  or or_9 (N6, and_31_out, and_32_out, and_33_out, and_34_out, and_35_out, and_41_out, and_36_out, and_37_out, and_42_out, and_38_out, and_43_out, and_39_out, and_44_out);
endmodule

module mux4x2 (
  input  A0,
  input  B0,
  input  A1,
  input  B1,
  input  A2,
  input  B2,
  input  A3,
  input  B3,
  input  S,
  output S0,
  output S1,
  output S2,
  output S3
);

  wire and_1_out, and_2_out, and_3_out, and_4_out, and_5_out, and_6_out, and_7_out, and_8_out, not_1_out;

  not not_1 (not_1_out, S);
  and and_1 (and_1_out, A0, not_1_out);
  and and_2 (and_2_out, B0, S);
  and and_3 (and_3_out, A1, not_1_out);
  and and_4 (and_4_out, B1, S);
  and and_5 (and_5_out, A2, not_1_out);
  and and_6 (and_6_out, B2, S);
  and and_7 (and_7_out, A3, not_1_out);
  and and_8 (and_8_out, B3, S);
  or or_1 (S0, and_1_out, and_2_out);
  or or_2 (S1, and_3_out, and_4_out);
  or or_3 (S2, and_5_out, and_6_out);
  or or_4 (S3, and_7_out, and_8_out);
endmodule

module Comp2 (
  input  X,
  input  B1,
  input  B0,
  input  A6,
  input  A5,
  input  A4,
  input  A3,
  input  A2,
  input  A1,
  input  A0,
  output out_11
);

  wire and_1_out, and_2_out, and_3_out, and_4_out, and_5_out, not_1_out, not_2_out, not_3_out, not_4_out,
       not_5_out, not_6_out, not_7_out, not_8_out, not_9_out, or_1_out, or_2_out;

  not not_1 (not_1_out, B1);
  not not_2 (not_2_out, B0);
  not not_3 (not_3_out, A6);
  not not_4 (not_4_out, A5);
  not not_5 (not_5_out, A4);
  not not_6 (not_6_out, A3);
  not not_7 (not_7_out, A2);
  not not_8 (not_8_out, A1);
  not not_9 (not_9_out, A0);
  and and_1 (and_1_out, not_3_out, not_4_out, not_5_out, not_6_out, not_7_out);
  and and_2 (and_2_out, not_1_out, B0, not_8_out, not_9_out);
  and and_3 (and_3_out, B1, not_2_out, not_8_out);
  and and_4 (and_4_out, not_8_out, A0);
  or or_1 (or_1_out, and_2_out, and_5_out, and_3_out);
  or or_2 (or_2_out, and_4_out, not_9_out);
  and and_5 (and_5_out, B1, B0, or_2_out);
  and and_6 (out_11, X, and_1_out, or_1_out, or_1_out);
endmodule

module decodBC7Segs (
  input  N0,
  input  N1,
  input  N2,
  input  N3,
  output A,
  output B,
  output C,
  output D,
  output E,
  output F,
  output G
);

  wire and_1_out, and_2_out, and_3_out, and_4_out, and_5_out, and_6_out, and_7_out, not_1_out, not_2_out,
       not_3_out, not_4_out, or_1_out;

  not not_1 (not_1_out, N0);
  not not_2 (not_2_out, N2);
  not not_3 (not_3_out, N1);
  not not_4 (not_4_out, N3);
  and and_1 (and_1_out, not_4_out, not_2_out, N1, not_1_out);
  and and_2 (and_2_out, not_4_out, not_2_out, N1, N0);
  and and_3 (and_3_out, not_4_out, N2, not_3_out, N0);
  and and_4 (and_4_out, not_4_out, N2, N1, not_1_out);
  and and_5 (and_5_out, not_4_out, N2, N1, N0);
  and and_6 (and_6_out, N3, not_2_out, not_3_out, not_1_out);
  and and_7 (and_7_out, N3, not_2_out, not_3_out, N0);
  or or_1 (or_1_out, and_1_out, and_2_out, and_3_out, and_4_out, and_5_out);
  or or_2 (A, or_1_out, and_6_out, and_7_out);
  // AND_Gate and_8 has open pins: in0=not_4_out, out=open

  // Notes on the sheet:
  //   A
  //   C
  //   B
  //   D
endmodule

module mux16para4 (
  input  in_1,
  input  in_2,
  input  in_3,
  input  in_4,
  input  in_5,
  input  in_6,
  input  in_7,
  input  in_8,
  input  in_9,
  input  in_10,
  input  in_11,
  input  in_12,
  input  in_13,
  input  in_14,
  input  in_15,
  input  in_16,
  input  in_17,
  input  in_18,
  output out_19,
  output out_20,
  output out_21,
  output out_22
);

  wire mux4x2_1_s0, mux4x2_1_s1, mux4x2_1_s2, mux4x2_1_s3, mux4x2_2_s0, mux4x2_2_s1, mux4x2_2_s2, mux4x2_2_s3;

  mux4x2 mux4x2_1 (
    .A0(in_1), .B0(in_5), .A1(in_2), .B1(in_6), .A2(in_3), .B2(in_7), .A3(in_4), .B3(in_8), .S(in_9),
    .S0(mux4x2_1_s0), .S1(mux4x2_1_s1), .S2(mux4x2_1_s2), .S3(mux4x2_1_s3));
  mux4x2 mux4x2_2 (
    .A0(in_11), .B0(in_15), .A1(in_12), .B1(in_16), .A2(in_13), .B2(in_17), .A3(in_14), .B3(in_18), .S(in_9),
    .S0(mux4x2_2_s0), .S1(mux4x2_2_s1), .S2(mux4x2_2_s2), .S3(mux4x2_2_s3));
  mux4x2 mux4x2_3 (
    .A0(mux4x2_1_s0), .B0(mux4x2_2_s0), .A1(mux4x2_1_s1), .B1(mux4x2_2_s1), .A2(mux4x2_1_s2),
    .B2(mux4x2_2_s2), .A3(mux4x2_1_s3), .B3(mux4x2_2_s3), .S(in_10), .S0(out_19), .S1(out_20), .S2(out_21),
    .S3(out_22));
endmodule

module SomadorComreg (
  input  in_1,
  input  in_2,
  input  in_3,
  input  in_4,
  input  in_5,
  input  in_6,
  input  in_7,
  input  in_8,
  input  in_9,
  output out_10,
  output out_11,
  output out_12,
  output out_13,
  output out_14,
  output out_15,
  output out_16,
  output out_17,
  output out_18
);

  wire and_1_out, botoes_1_n0, botoes_1_n1, not_1_out, not_2_out, not_3_out, not_4_out, not_5_out, not_6_out,
       not_7_out, not_8_out, not_9_out, not_10_out, not_11_out, not_12_out, not_13_out, not_14_out,
       not_15_out, not_16_out, not_17_out, not_18_out, not_19_out, not_20_out, not_21_out, not_22_out,
       not_23_out, not_24_out, not_25_out, not_26_out, not_27_out, not_28_out, not_29_out, not_30_out,
       not_31_out, not_32_out, not_33_out, not_34_out, not_35_out, not_36_out, not_37_out, not_38_out,
       not_39_out, not_40_out, not_41_out, not_42_out, or_1_out, somador_subtrator_1_s2,
       somador_subtrator_1_s3, somador_subtrator_1_s4, somador_subtrator_1_s5, somador_subtrator_1_s6;

  not not_1 (not_1_out, not_2_out);
  not not_2 (not_2_out, not_35_out);
  not not_3 (not_3_out, not_4_out);
  not not_4 (not_4_out, not_39_out);
  not not_5 (not_5_out, not_6_out);
  not not_6 (not_6_out, not_1_out);
  not not_7 (not_7_out, not_8_out);
  not not_8 (not_8_out, not_3_out);
  Botoes botoes_1 (.A(in_1), .B(in_3), .C(in_4), .N0(botoes_1_n0), .N1(botoes_1_n1));  // open: Ch0, out_7
  not not_9 (not_9_out, or_1_out);
  not not_10 (not_10_out, not_31_out);
  not not_11 (not_11_out, not_34_out);
  not not_12 (not_12_out, not_13_out);
  not not_13 (not_13_out, not_5_out);
  not not_14 (not_14_out, not_12_out);
  not not_15 (not_15_out, not_16_out);
  not not_16 (not_16_out, not_7_out);
  not not_17 (not_17_out, not_15_out);
  not not_18 (not_18_out, not_20_out);
  not not_19 (not_19_out, not_9_out);
  not not_20 (not_20_out, not_19_out);
  not not_21 (not_21_out, not_23_out);
  not not_22 (not_22_out, not_21_out);
  not not_23 (not_23_out, not_10_out);
  not not_24 (not_24_out, not_25_out);
  not not_25 (not_25_out, not_26_out);
  not not_26 (not_26_out, not_11_out);
  not not_27 (not_27_out, not_28_out);
  not not_28 (not_28_out, not_14_out);
  not not_29 (not_29_out, not_17_out);
  not not_30 (not_30_out, not_29_out);
  not not_31 (not_31_out, not_32_out);
  not not_32 (not_32_out, not_18_out);
  not not_33 (not_33_out, not_22_out);
  not not_34 (not_34_out, not_33_out);
  not not_35 (not_35_out, not_36_out);
  not not_36 (not_36_out, not_24_out);
  not not_37 (not_37_out, not_27_out);
  not not_38 (not_38_out, not_37_out);
  not not_39 (not_39_out, not_38_out);
  not not_40 (not_40_out, not_41_out);
  not not_41 (not_41_out, not_42_out);
  not not_42 (not_42_out, not_30_out);
  or or_1 (or_1_out, botoes_1_n0, botoes_1_n1);
  Somador_Subtrator somador_subtrator_1 (
    .Ci(in_2), .A0(out_10), .B0(botoes_1_n0), .A1(out_11), .B1(botoes_1_n1), .A2(out_12), .B2(in_5),
    .A3(out_13), .B3(in_6), .A4(out_14), .B4(in_7), .A5(out_15), .B5(in_8), .A6(out_16), .B6(in_9),
    .S0(out_17), .S1(out_18), .S2(somador_subtrator_1_s2), .S3(somador_subtrator_1_s3),
    .S4(somador_subtrator_1_s4), .S5(somador_subtrator_1_s5), .S6(somador_subtrator_1_s6));  // open: Cout
  and and_1 (and_1_out, or_1_out, not_40_out);
  D_Flip_Flop d_ff_1 (.clk(and_1_out), .D(out_17), .Q(out_10));  // open: Qn, preset, en, reset
  D_Flip_Flop d_ff_2 (.clk(and_1_out), .D(out_18), .Q(out_11));  // open: Qn, preset, en, reset
  D_Flip_Flop d_ff_3 (.clk(and_1_out), .D(somador_subtrator_1_s2), .Q(out_12));  // open: Qn, preset, en, reset
  D_Flip_Flop d_ff_4 (.clk(and_1_out), .D(somador_subtrator_1_s3), .Q(out_13));  // open: Qn, preset, en, reset
  D_Flip_Flop d_ff_5 (.clk(and_1_out), .D(somador_subtrator_1_s4), .Q(out_14));  // open: Qn, preset, en, reset
  D_Flip_Flop d_ff_6 (.clk(and_1_out), .D(somador_subtrator_1_s5), .Q(out_15));  // open: Qn, preset, en, reset
  D_Flip_Flop d_ff_7 (.clk(and_1_out), .D(somador_subtrator_1_s6), .Q(out_16));  // open: Qn, preset, en, reset
endmodule
